# Fritzing sketch GPRS_SD_Pot (saved by Fritzing 0.8.5b)
breadboards: 1

parts:
  Part1 = Arduino Uno (Rev3)
  R1 = Rotary Potentiometer (Small) [maximum_resistance=100kΩ package=THT]
  R2 = Resistor [tolerance=±5% resistance=10k package=THT]
  Part2 = Arduino Cellular Shield
  Part3 = Arduino MicroSD Shield

nets:
  N1: Part1.A0, R1.wiper
  N2: Part1.D8, Part2.D8
  N3: Part1.D9_PWM, Part2.D9
  N4: Part1.D10_PWM/SS, Part3.D10
  N5: Part1.GND, R1.leg1
  N6: Part1.D7, Part2.D7
  N7: Part1.5V, R2.Pin_0
  N8: R1.leg2, R2.Pin_1

notes:
  (Shields displayed unstacked to show pin use)
  SeeedStudio GPRS Shield v1.0 (Sparkfun shown)
  SeeedStudio SD Shield (Sparkfun shown)
  H2O Level Monitor:
  - Reads H2O level (mimicked by potentiometer for development) at regular interval and writes to SD. If change detected before scheduled write, checks again to confirm, then writes. Also pulls date/time from GPRS, parses, and writes with H2O level.

// code stored in the sketch: MERGE_DTH2O_WriteIfChange_11414_947pm.ino
/*  Framework for debugging individual program elements  */

#include <SoftwareSerial.h>
#include <SD.h>

#define rxPin 7
#define txPin 8
#define powPin 9

const int chipSelect = 10;

SoftwareSerial gprsSerial(rxPin, txPin);

String rawDateTime;
String timeString;
String dateString;
String fullDataString;

int h2oLevel = 0;
int h2oLastLevel = 0;
const int h2oChangeTrigger = 5;

unsigned long currTimer = 0;
unsigned long prevTimer = 0;
unsigned long interval = 30000;

void setup() {
  pinMode(rxPin, INPUT);
  pinMode(txPin, OUTPUT);
  pinMode(powPin, OUTPUT);
  pinMode(10, OUTPUT);  // Required for SD lib fxn

  Serial.begin(19200);
  gprsSerial.begin(19200);

  powerUp();
  gprsBootLoop();

  h2oLevelRead();
  h2oLastLevel = h2oLevel;

  if (!SD.begin(chipSelect)) {
    Serial.println("Card failed, or not present.");
    return;
  }
  Serial.println("SD card initialized.");
  Serial.println();
}

void loop() {
  currTimer = millis();
  Serial.print("Last measured water level: ");
  Serial.println(h2oLastLevel);
  h2oLevelRead();
  Serial.print("Current water level: ");
    Serial.println(h2oLevel);
  if((currTimer - prevTimer) < interval) {
    if(abs(h2oLevel - h2oLastLevel) <= h2oChangeTrigger) {
      int nextWrite = (interval - (currTimer - prevTimer)) / 1000;
      Serial.print("Next measurement in ");
      Serial.print(nextWrite);
      Serial.println(" seconds.");
      Serial.println();
    }
    else {
      Serial.println("Water level change >5% detected. Reading again to confirm.");
      delay(5000);
      h2oLevelRead();
      if(abs(h2oLevel - h2oLastLevel) >= h2oChangeTrigger) {
        Serial.println("Change confirmed. Writing to SD card.");
        h2oWriteSD();
        prevTimer = currTimer;
      }
      else {
        Serial.println("Detected change was a false-positive.");
      }
    }
  }
  delay(2000);
}

void clearStrings() {
  dateString = "";
  timeString = "";
  fullDataString = "";
}

void concatStrings() {
  fullDataString += dateString;
  fullDataString += ",";
  fullDataString += timeString;
  fullDataString += ",";
  fullDataString += h2oLevel;
}

void gprsBootLoop() {
  while(dateString == 0) {
    getDateTime();
    delay(1000);
  }
  //dateLong();
  //Serial.println(dateLongString);
  clearStrings();
}

// Software start-up function for GPRS shield
void powerUp() {
  digitalWrite(powPin, LOW);
  delay(100);
  digitalWrite(powPin, HIGH);
  delay(500);
  digitalWrite(powPin, LOW);
  delay(100);
}

void getDateTime() {
  gprsSerial.println("AT+CCLK?");  // Request date and time from GPRS
  if(gprsSerial.available()) {  // If data is coming from GPRS
    while(gprsSerial.available()) {  // Read the data into string from incoming bytes while they're available
      char c = gprsSerial.read();  // Read each byte sent, one at a time, into storage variable
      rawDateTime += c;  // Add character to the end of the data string to be written to SD later
    }
    parseDateTime();
  }
}

void parseDateTime() {
  String year = "";
  String month = "";
  String day = "";

  for(int y = 8; y < 10; y++)
    year += String(rawDateTime.charAt(y));
  for(int m = 11; m < 13; m++)
    month += String(rawDateTime.charAt(m));
  for(int d = 14; d < 16; d++)
    day += String(rawDateTime.charAt(d));
  for(int t = 17; t < 25; t++)
    timeString += String(rawDateTime.charAt(t));

  rawDateTime = "";

  dateString += String(month);
  dateString += "/";
  dateString += String(day);
  dateString += "/";
  dateString += String(year);
}

void h2oLevelRead() {
  int h2oReadVal = analogRead(A0);
  h2oLevel = h2oReadVal / 9.22;  // Divide by (MaximumPossibleReading / 100) for 0-100 scale
}

void h2oWriteSD() {
  getDateTime();
  concatStrings();
  sdWriteData();
  Serial.println();
  clearStrings();
  h2oLastLevel = h2oLevel;
}

void sdWriteData() {
  File dataFile = SD.open("NEWDATA.TXT", FILE_WRITE);  // Open data file, with full privileges, for writing
  if(dataFile) {  // If file on SD card is opened successfully
    dataFile.println(fullDataString);  // Print dataString to it
    dataFile.close();  // Close the data file and proceed
    Serial.println(fullDataString);
  }
  else {
    Serial.println("Error opening file while attempting to write to SD.");  // If data file can't be opened, produce an error message
  }
}
